# Fritzing sketch Circuit_1 (saved by Fritzing 0.9.3b)
circuit board: 8.46667cm x 5.64444cm
breadboards: 1

parts:
  SPDT_RELAY = RELAY [package=relay-t9a]
  1N4148 = Rectifier Diode [part_number=1N4001 package="300 mil [THT]"]
  BC557 = PNP-Transistor [package="TO92 [THT]"]
  R1 = Resistor [tolerance=±5% resistance=22k package=THT]
  R2 = Resistor [tolerance=±5% resistance=2.2k package=THT]
  220U = Capacitor Polarized [package=cpol-radial-1000uf-25v]
  1N4148_2 = Rectifier Diode [part_number=1N4001 package="300 mil [THT]"]
  BC547 = NPN-Transistor [package="TO92 [THT]"]
  R3 = Resistor [tolerance=±5% resistance=10k package=THT]
  R4 = Resistor [tolerance=±5% resistance=10k package=THT]
  U1 = NodeMCU V1.0
  F1 = FUSE [package=fuse_5mm]
  L1 = Inductor [package="400 mil [THT]"]

nets:
  N1: SPDT_RELAY.COIL1, 1N4148.cathode, BC557.C
  N2: SPDT_RELAY.COIL2, 1N4148.anode, 220U.-, 1N4148_2.anode
  N3: SPDT_RELAY.MAIN, F1.2
  N4: SPDT_RELAY.NO, L1.pin_1
  5V: BC557.E, R2.Pin_0, U1.Vin
  N5: BC557.B, R1.Pin_1
  N6: R1.Pin_0, R2.Pin_1, 220U.+, BC547.C
  GND: 1N4148_2.cathode, BC547.E, R3.Pin_1, U1.GND
  N7: BC547.B, R3.Pin_0, R4.Pin_0
  N8: R4.Pin_1, U1.D1
  220V AC: F1.1
  NEUTRAL: L1.pin_0

custom parts:
  NodeMCU V1.0: ESP8266 based NodeMCU
