# Fritzing sketch Circuit_2 (saved by Fritzing 0.9.3b)
breadboards: 1

parts:
  Opto-Coupler_U1 = Optocoupler [package=THT]
  Opto-Isolated_Triac_U2 = MOC3031-M [package=dil06]
  R1 = Resistor [tolerance=±5% resistance=10k package=THT]
  U3 = NodeMCU V1.0
  R2 = Resistor [tolerance=±5% resistance=220 package=THT]
  400V_Bridge_Rectifier_D1 = bridge rectifier round [package="round [THT]"]
  220V = Screw terminal - 2 pins [package=THT]
  R3 = Resistor [tolerance=±5% resistance=1k package=THT]
  U4 = TRIAC [package=to-92]
  LOAD = Screw terminal - 2 pins [package=THT]
  30k_1/2_Watt = Resistor [tolerance=±5% resistance=1k package=THT]
  30k_1/2_Watt_2 = Resistor [tolerance=±5% resistance=1k package=THT]

nets:
  N1: Opto-Coupler_U1.Pin_1, 400V_Bridge_Rectifier_D1.DC+
  N2: Opto-Coupler_U1.Pin_2, 400V_Bridge_Rectifier_D1.DC-
  GND: Opto-Coupler_U1.Pin_4
  N3: Opto-Coupler_U1.Pin_5, R1.Pin_1, U3.D1
  N4: Opto-Isolated_Triac_U2.1, R2.Pin_1
  N5: Opto-Isolated_Triac_U2.2, U3.GND
  N6: Opto-Isolated_Triac_U2.4, U4.G
  N7: Opto-Isolated_Triac_U2.6, R3.Pin_0
  5V: R1.Pin_0
  N8: U3.D2, R2.Pin_0
  N9: 400V_Bridge_Rectifier_D1.AC#0, 30k_1/2_Watt_2.Pin_0
  N10: 400V_Bridge_Rectifier_D1.AC#1, 30k_1/2_Watt.Pin_0
  N11: 220V.pin1, R3.Pin_1, U4.M2, 30k_1/2_Watt.Pin_1
  N12: 220V.pin2, LOAD.pin1, 30k_1/2_Watt_2.Pin_1
  N13: U4.M1, LOAD.pin2

notes:
  Zero Crossing Signal Out
  Dimmer Signal In

custom parts:
  NodeMCU V1.0: ESP8266 based NodeMCU
